# Fritzing sketch PushButtonLED (saved by Fritzing 0.9.3b)
breadboards: 1

parts:
  Part1 = Arduino Mega 2560 (Rev3)
  LED1 = LED - 5mm [color="Red (635nm)" package="5 mm [THT]"]
  R1 = Resistor [tolerance=±5% resistance=220 package="2010 [SMD]"]
  S1 = Pushbutton [package="[SMD]"]
  R2 = Resistor [tolerance=±5% resistance=220 package="2010 [SMD]"]
  J1 = Piezo Speaker  # not connected

nets:
  N1: Part1.D15/RX3, S1.Pin_3, S1.Pin_4, R2.Pin_1
  N2: Part1.D14/TX3, LED1.anode
  N3: Part1.GND, R1.Pin_0, R2.Pin_0
  N4: Part1.5V, S1.Pin_1, S1.Pin_2
  N5: LED1.cathode, R1.Pin_1
